# Fritzing sketch otopark (saved by Fritzing 0.9.3b)
breadboards: 1

parts:
  Parça1 = Bluetooth HC-05 Macho
  Parça2 = Arduino Mega 2560 (Rev3)
  Parça3 = RFID-RC522-v2
  LED1 = RGB LED (com. cathode, rbg) [package="5 mm [THT]"]
  J1 = Piezo Speaker
  LCD1 = LCD screen
  RE1 = Rotary Encoder [package=THT]
  J2 = Basic Servo
  J3 = Basic Servo

nets:
  N1: Parça1.TXD, Parça2.D0_RX0
  N2: Parça1.RXD, Parça2.D1_TX0
  VCC: Parça1.VCC, Parça2.5V, LCD1.VDD, LCD1.LED+, RE1.EncoderPinB, J2.vcc, J3.vcc
  GND: Parça1.GND, Parça2.GND, Parça3.GND, LED1.red_anode, J1.pin1, LCD1.VSS, LCD1.R/W, LCD1.LED-, RE1.EncoderPinA, J2.gnd, J3.gnd
  N3: Parça2.D12_PWM, LCD1.RS
  N4: Parça2.D11_PWM, LCD1.E
  N5: Parça2.D10_PWM, LED1.common_cathode
  N6: Parça2.D9_PWM, LED1.blue_anode
  N7: Parça2.D8_PWM, LED1.green_anode
  3V3: Parça2.3V3, Parça3.3.3V
  N8: Parça2.D4_PWM, LCD1.DB7
  N9: Parça2.D5_PWM, LCD1.DB6
  N10: Parça2.D6_PWM, LCD1.DB5
  N11: Parça2.D7_PWM, LCD1.DB4
  N12: Parça2.D49, Parça3.RST
  N13: Parça2.D50, Parça3.MISO
  N14: Parça2.D51, Parça3.MOSI
  N15: Parça2.D52, Parça3.SCK
  N16: Parça2.D53, Parça3.SDA
  N17: LCD1.V0, RE1.EncoderPinC

notes:
  servo motorlar
  hc05 bluetooth
  modülü
  rfid rc522
  okuyucu
  arduino mega
  2560
  buzzer
  rgb
  lcd ekran
  potansiyometre

custom parts:
  RFID-RC522-v2: A simple China made RFID-RC522 Reader; do check the pin labels, as this is a MFRC522 based clone.
